// Logisim project lab8.circ as structural Verilog: 2 circuits, main circuit main
module main (
  input  Cin,
  input  [3:0] in_2,
  input  [3:0] Y,
  output [4:0] out_4
);

  wire and_1_out, and_2_out, and_3_out, and_4_out, and_5_out, and_6_out, and_7_out, and_8_out, or_1_out,
       or_2_out, or_3_out, xor_1_out, xor_2_out, xor_3_out, xor_4_out;

  xor xor_1 (xor_1_out, in_2[0], Y[0]);
  and and_1 (and_1_out, in_2[0], Y[0]);
  xor xor_2 (xor_2_out, in_2[1], Y[1]);
  and and_2 (and_2_out, in_2[1], Y[1]);
  xor xor_3 (xor_3_out, in_2[2], Y[2]);
  and and_3 (and_3_out, in_2[2], Y[2]);
  xor xor_4 (xor_4_out, in_2[3], Y[3]);
  and and_4 (and_4_out, in_2[3], Y[3]);
  xor xor_5 (out_4[0], xor_1_out, Cin);
  and and_5 (and_5_out, xor_1_out, Cin);
  xor xor_6 (out_4[1], xor_2_out, or_1_out);
  and and_6 (and_6_out, xor_2_out, or_1_out);
  xor xor_7 (out_4[2], xor_3_out, or_2_out);
  and and_7 (and_7_out, xor_3_out, or_2_out);
  xor xor_8 (out_4[3], xor_4_out, or_3_out);
  and and_8 (and_8_out, xor_4_out, or_3_out);
  or or_1 (or_1_out, and_5_out, and_1_out);
  or or_2 (or_2_out, and_6_out, and_2_out);
  or or_3 (or_3_out, and_7_out, and_3_out);
  or or_4 (out_4[4], and_8_out, and_4_out);

  // Notes on the sheet:
  //   X
  //   Answer
endmodule

module full_adder (
  input  X,
  input  Y,
  input  Z,
  output S,
  output C
);

  wire and_1_out, and_2_out, xor_1_out;

  xor xor_1 (xor_1_out, X, Y);
  and and_1 (and_1_out, X, Y);
  xor xor_2 (S, xor_1_out, Z);
  and and_2 (and_2_out, xor_1_out, Z);
  or or_1 (C, and_2_out, and_1_out);
endmodule
